// Logisim project CSE-231 Pattern Based Digital Lock System.circ as structural Verilog: 14 circuits, main circuit main
module main (
);

  wire _0_out, _1_out, _2_out, _3_out, _4_out, _5_out, _6_out, _7_out, _8_out, _9_out, _10_to_4_bit_out_11,
       _10_to_4_bit_out_12, _10_to_4_bit_out_13, _10_to_4_bit_out_14, Counter_out_3, n7_segment_display_1_a,
       n7_segment_display_1_b2, n7_segment_display_1_c2, n7_segment_display_1_d2, n7_segment_display_1_e,
       n7_segment_display_1_f, n7_segment_display_1_g, or_1_out, output_display_1_a_2, output_display_1_b_2,
       output_display_1_c, output_display_1_d, output_display_1_e, output_display_1_f, output_display_1_g,
       pattern_checker_1_out_23, RESET___CLEAR_out;

  Button _0 (.out(_0_out));
  Button _3 (.out(_3_out));
  Button _6 (.out(_6_out));
  Button _9 (.out(_9_out));
  Button _2 (.out(_2_out));
  Button _1 (.out(_1_out));
  Button _4 (.out(_4_out));
  Button _5 (.out(_5_out));
  Button _7 (.out(_7_out));
  Button _8 (.out(_8_out));
  Button RESET___CLEAR (.out(RESET___CLEAR_out));
  _7_segment_display u_7_segment_display_1 (
    .d(_10_to_4_bit_out_14), .c(_10_to_4_bit_out_13), .b(_10_to_4_bit_out_12), .a2(_10_to_4_bit_out_11),
    .a(n7_segment_display_1_a), .b2(n7_segment_display_1_b2), .c2(n7_segment_display_1_c2),
    .d2(n7_segment_display_1_d2), .e(n7_segment_display_1_e), .f(n7_segment_display_1_f),
    .g(n7_segment_display_1_g));
  _16_4_priority_Encoder _10_to_4_bit (
    ._0(_0_out), ._1(_1_out), ._2(_2_out), ._3(_3_out), ._4(_4_out), ._5(_5_out), ._6(_6_out), ._7(_7_out),
    ._8(_8_out), ._9(_9_out), .out_11(_10_to_4_bit_out_11), .out_12(_10_to_4_bit_out_12),
    .out_13(_10_to_4_bit_out_13), .out_14(_10_to_4_bit_out_14));
  or or_1 (or_1_out, _10_to_4_bit_out_14, _10_to_4_bit_out_13, _10_to_4_bit_out_12, _10_to_4_bit_out_11);
  _7_Segment_Display u_7_segment_display_2 (
    .g(n7_segment_display_1_g), .f(n7_segment_display_1_f), .a(n7_segment_display_1_a),
    .b(n7_segment_display_1_b2), .e(n7_segment_display_1_e), .d(n7_segment_display_1_d2),
    .c(n7_segment_display_1_c2));  // open: dp
  Pattern_checker pattern_checker_1 (
    .in_1(or_1_out), .in_2(Counter_out_3), .in_19(_10_to_4_bit_out_14), .in_20(_10_to_4_bit_out_13),
    .in_21(_10_to_4_bit_out_12), .in_22(_10_to_4_bit_out_11), .in_3(_10_to_4_bit_out_14),
    .in_4(_10_to_4_bit_out_13), .in_5(_10_to_4_bit_out_12), .in_6(_10_to_4_bit_out_11),
    .in_7(_10_to_4_bit_out_14), .in_8(_10_to_4_bit_out_13), .in_9(_10_to_4_bit_out_12),
    .in_10(_10_to_4_bit_out_11), .out_23(pattern_checker_1_out_23), .in_11(_10_to_4_bit_out_14),
    .in_12(_10_to_4_bit_out_13), .in_13(_10_to_4_bit_out_12), .in_14(_10_to_4_bit_out_11),
    .in_15(_10_to_4_bit_out_14), .in_16(_10_to_4_bit_out_13), .in_17(_10_to_4_bit_out_12),
    .in_18(_10_to_4_bit_out_11));
  LED led_1 (.in(Counter_out_3));
  Counter_2 Counter (.in_1(or_1_out), .out_3(Counter_out_3), .in_2(RESET___CLEAR_out));
  Output_Display output_display_1 (
    .A(pattern_checker_1_out_23), .B(Counter_out_3), .a_2(output_display_1_a_2), .b_2(output_display_1_b_2),
    .c(output_display_1_c), .d(output_display_1_d), .e(output_display_1_e), .f(output_display_1_f),
    .g(output_display_1_g));
  _7_Segment_Display u_7_segment_display_3 (
    .g(output_display_1_g), .f(output_display_1_f), .a(output_display_1_a_2), .b(output_display_1_b_2),
    .e(output_display_1_e), .d(output_display_1_d), .c(output_display_1_c));  // open: dp

  // Notes on the sheet:
  //   KEYPAD
  //   5 - Digit Pattern Checker (54042) 
  //   Input Display
  //   Space Available
endmodule

// priority encoder
module _16_4_priority_Encoder (
  input  _0,
  input  _1,
  input  _2,
  input  _3,
  input  _4,
  input  _5,
  input  _6,
  input  _7,
  input  _8,
  input  _9,
  output out_11,
  output out_12,
  output out_13,
  output out_14
);

  wire and_1_out, and_2_out, and_3_out, and_4_out, and_5_out, and_6_out, and_7_out, and_8_out, and_9_out,
       and_10_out, and_11_out, not_1_out, not_2_out, not_3_out, not_4_out, not_5_out, not_6_out, not_7_out,
       not_8_out, not_9_out, not_10_out, not_11_out, or_1_out, or_2_out, or_3_out, or_4_out, or_7_out;

  not not_1 (not_1_out, _2);
  not not_2 (not_2_out, _3);
  not not_3 (not_3_out, _6);
  not not_4 (not_4_out, _7);
  not not_5 (not_5_out, _4);
  not not_6 (not_6_out, _6);
  not not_7 (not_7_out, _8);
  or or_1 (or_1_out, _0, _1);
  or or_2 (or_2_out, _4, _5);
  and and_1 (and_1_out, not_1_out, not_2_out);
  and and_2 (and_2_out, not_3_out, not_4_out);
  and and_3 (and_3_out, not_5_out, not_6_out, not_7_out);
  and and_4 (and_4_out, _5, not_6_out);
  and and_5 (and_5_out, and_3_out, or_4_out);
  and and_6 (and_6_out, or_1_out, and_8_out);
  and and_7 (and_7_out, or_2_out, and_2_out);
  and and_8 (and_8_out, and_1_out, and_2_out);
  and and_9 (and_9_out, _1, not_1_out);
  or or_3 (or_3_out, and_4_out, _7);
  not not_8 (not_8_out, _9);
  not not_9 (not_9_out, _8);
  not not_10 (not_10_out, _7);
  not not_11 (not_11_out, _6);
  or or_4 (or_4_out, and_9_out, _3);
  and and_10 (and_10_out, or_3_out, not_7_out);
  and and_11 (and_11_out, not_8_out, not_9_out, not_10_out, not_11_out);
  or or_5 (out_11, _9, and_10_out, and_5_out);
  or or_6 (out_12, and_6_out, and_7_out, _8, _9);
  or or_7 (or_7_out, _2, _3, _4, _5);
  or or_8 (out_14, _6, _7, _8, _9);
  and and_12 (out_13, or_7_out, and_11_out);

  // Notes on the sheet:
  //   A
  //   B
  //   C
  //   D
endmodule

// comparator
module _4_bit_comparator (
  input  A,
  input  B,
  input  C,
  input  D,
  input  a_2,
  input  b_2,
  input  E,
  input  c_2,
  input  d_2,
  output out_10
);

  wire xnor_1_out, xnor_2_out, xnor_3_out, xnor_4_out;

  xnor xnor_1 (xnor_1_out, A, a_2);
  xnor xnor_2 (xnor_2_out, B, b_2);
  xnor xnor_3 (xnor_3_out, C, c_2);
  xnor xnor_4 (xnor_4_out, D, d_2);
  and and_1 (out_10, xnor_1_out, xnor_2_out, E, xnor_3_out, xnor_4_out);
endmodule

module Output_Display (
  input  A,
  input  B,
  output a_2,
  output b_2,
  output c,
  output d,
  output e,
  output f,
  output g
);

  or or_1 (d, B, A);
  or or_2 (e, B, A);
  or or_3 (f, B, A);

  assign a_2 = 1'b0;
  assign b_2 = A;
  assign c = A;
  assign g = 1'b0;
endmodule

// 7 segment
module _7_segment_display (
  input  d,
  input  c,
  input  b,
  input  a2,
  output a,
  output b2,
  output c2,
  output d2,
  output e,
  output f,
  output g
);

  wire and_1_out, and_2_out, and_3_out, and_4_out, and_5_out, and_6_out, and_7_out, and_8_out, and_9_out,
       and_10_out, and_11_out, and_12_out, and_13_out, and_14_out, and_15_out, and_16_out, and_17_out,
       and_18_out, and_19_out, and_20_out, and_21_out, and_22_out, not_1_out, not_2_out, not_3_out,
       not_4_out, not_5_out, not_6_out, not_7_out, not_8_out, not_9_out, not_10_out, not_11_out, not_12_out,
       not_13_out, not_14_out, not_15_out, not_16_out, not_17_out, not_18_out;

  not not_1 (not_1_out, c);
  and and_1 (and_1_out, not_1_out, b, not_2_out);
  not not_2 (not_2_out, a2);
  and and_2 (and_2_out, c, not_3_out);
  not not_3 (not_3_out, b);
  and and_3 (and_3_out, c, a2);
  not not_4 (not_4_out, c);
  and and_4 (and_4_out, not_4_out, b);
  and and_5 (and_5_out, c, not_5_out);
  not not_5 (not_5_out, b);
  and and_6 (and_6_out, c, not_6_out);
  not not_6 (not_6_out, a2);
  and and_7 (and_7_out, d, a2);
  and and_8 (and_8_out, c, a2);
  not not_7 (not_7_out, c);
  and and_9 (and_9_out, not_7_out, b, not_8_out);
  not not_8 (not_8_out, a2);
  and and_10 (and_10_out, c, not_9_out);
  not not_9 (not_9_out, b);
  and and_11 (and_11_out, c, a2);
  and and_12 (and_12_out, d, not_10_out);
  not not_10 (not_10_out, a2);
  and and_13 (and_13_out, d, b);
  not not_11 (not_11_out, c);
  and and_14 (and_14_out, not_11_out, b, not_12_out);
  not not_12 (not_12_out, a2);
  and and_15 (and_15_out, c, not_13_out, not_14_out);
  not not_13 (not_13_out, b);
  not not_14 (not_14_out, a2);
  and and_16 (and_16_out, d, not_15_out);
  not not_15 (not_15_out, a2);
  and and_17 (and_17_out, b, not_16_out);
  not not_16 (not_16_out, a2);
  and and_18 (and_18_out, c, b);
  and and_19 (and_19_out, d, not_17_out);
  not not_17 (not_17_out, a2);
  and and_20 (and_20_out, d, b);
  and and_21 (and_21_out, d, not_18_out);
  not not_18 (not_18_out, a2);
  and and_22 (and_22_out, d, b);
  or or_1 (a, and_1_out, and_2_out, and_3_out, d);
  or or_2 (b2, and_4_out, and_5_out, and_6_out, and_7_out);
  or or_3 (c2, b, and_8_out, d);
  or or_4 (d2, and_9_out, and_10_out, and_11_out, and_12_out, and_13_out);
  or or_5 (e, and_14_out, and_15_out, and_16_out);
  or or_6 (f, and_17_out, and_18_out, and_19_out, and_20_out);
  or or_7 (g, c, and_21_out, and_22_out);
endmodule

module Seq_1 (
  input  X,
  input  in_2,
  output Z
);

  wire and_1_out, and_2_out, and_3_out, and_4_out, and_5_out, and_6_out, and_7_out, and_8_out, and_9_out,
       d_ff_1_q, d_ff_2_q, d_ff_3_q, not_1_out, not_2_out, not_3_out, not_4_out, not_5_out, not_6_out,
       not_7_out, not_8_out, or_2_out, or_3_out, or_4_out;

  not not_1 (not_1_out, X);
  not not_2 (not_2_out, X);
  not not_3 (not_3_out, d_ff_2_q);
  not not_4 (not_4_out, X);
  not not_5 (not_5_out, d_ff_3_q);
  not not_6 (not_6_out, d_ff_1_q);
  not not_7 (not_7_out, d_ff_3_q);
  not not_8 (not_8_out, X);
  and and_1 (and_1_out, d_ff_1_q, not_1_out);
  or or_1 (Z, and_1_out, and_2_out);
  and and_2 (and_2_out, d_ff_1_q, d_ff_2_q);
  and and_3 (and_3_out, d_ff_2_q, d_ff_3_q, not_2_out);
  or or_2 (or_2_out, and_3_out, and_4_out);
  and and_4 (and_4_out, d_ff_1_q, X);
  and and_5 (and_5_out, not_3_out, d_ff_3_q, not_4_out);
  or or_3 (or_3_out, and_5_out, and_6_out, and_7_out);
  and and_6 (and_6_out, d_ff_2_q, not_5_out);
  and and_7 (and_7_out, d_ff_2_q, X);
  and and_8 (and_8_out, not_6_out, not_7_out, not_8_out);
  or or_4 (or_4_out, and_8_out, and_9_out);
  and and_9 (and_9_out, d_ff_3_q, X);
  D_Flip_Flop d_ff_1 (.clk(in_2), .D(or_2_out), .Q(d_ff_1_q));  // open: Qn, preset, en, reset
  D_Flip_Flop d_ff_2 (.clk(in_2), .D(or_3_out), .Q(d_ff_2_q));  // open: Qn, preset, en, reset
  D_Flip_Flop d_ff_3 (.clk(in_2), .D(or_4_out), .Q(d_ff_3_q));  // open: Qn, preset, en, reset
endmodule

module Seq_2 (
  input  X,
  input  in_2,
  output Z
);

  wire and_1_out, and_2_out, and_3_out, and_4_out, and_5_out, and_6_out, and_7_out, d_ff_1_q, d_ff_2_q,
       d_ff_3_q, not_1_out, not_2_out, not_3_out, not_4_out, not_5_out, not_6_out, not_7_out, or_2_out,
       or_3_out;

  and and_1 (and_1_out, d_ff_1_q, not_1_out);
  not not_1 (not_1_out, X);
  and and_2 (and_2_out, d_ff_1_q, d_ff_2_q);
  and and_3 (and_3_out, d_ff_2_q, d_ff_3_q, X);
  and and_4 (and_4_out, d_ff_3_q, not_2_out);
  not not_2 (not_2_out, X);
  and and_5 (and_5_out, d_ff_2_q, not_3_out);
  not not_3 (not_3_out, d_ff_3_q);
  not not_4 (not_4_out, d_ff_1_q);
  not not_5 (not_5_out, d_ff_2_q);
  and and_6 (and_6_out, not_4_out, not_5_out, X);
  not not_6 (not_6_out, d_ff_1_q);
  and and_7 (and_7_out, not_6_out, not_7_out, X);
  not not_7 (not_7_out, d_ff_3_q);
  or or_1 (Z, and_1_out, and_2_out);
  or or_2 (or_2_out, and_4_out, and_5_out);
  or or_3 (or_3_out, and_6_out, and_7_out);
  D_Flip_Flop d_ff_1 (.clk(in_2), .D(and_3_out), .Q(d_ff_1_q));  // open: Qn, preset, en, reset
  D_Flip_Flop d_ff_2 (.clk(in_2), .D(or_2_out), .Q(d_ff_2_q));  // open: Qn, preset, en, reset
  D_Flip_Flop d_ff_3 (.clk(in_2), .D(or_3_out), .Q(d_ff_3_q));  // open: Qn, preset, en, reset
endmodule

module Seq_3 (
  input  X,
  input  in_2,
  output Z
);

  wire and_2_out, and_3_out, and_4_out, and_5_out, and_6_out, and_7_out, d_ff_1_q, d_ff_2_q, d_ff_3_q,
       not_1_out, not_2_out, not_3_out, not_4_out, not_5_out, not_6_out, not_7_out, or_1_out, or_2_out;

  and and_1 (Z, d_ff_1_q, X);
  and and_2 (and_2_out, d_ff_2_q, d_ff_3_q, X);
  not not_1 (not_1_out, X);
  not not_2 (not_2_out, X);
  not not_3 (not_3_out, X);
  not not_4 (not_4_out, d_ff_1_q);
  not not_5 (not_5_out, d_ff_2_q);
  not not_6 (not_6_out, d_ff_3_q);
  not not_7 (not_7_out, X);
  and and_3 (and_3_out, d_ff_3_q, not_1_out);
  and and_4 (and_4_out, d_ff_2_q, not_2_out);
  and and_5 (and_5_out, d_ff_1_q, not_3_out);
  and and_6 (and_6_out, not_4_out, not_5_out, not_6_out, X);
  and and_7 (and_7_out, d_ff_2_q, not_7_out);
  or or_1 (or_1_out, and_3_out, and_4_out, and_5_out);
  or or_2 (or_2_out, and_6_out, and_7_out);
  D_Flip_Flop d_ff_1 (.clk(in_2), .D(and_2_out), .Q(d_ff_1_q));  // open: Qn, preset, en, reset
  D_Flip_Flop d_ff_2 (.clk(in_2), .D(or_1_out), .Q(d_ff_2_q));  // open: Qn, preset, en, reset
  D_Flip_Flop d_ff_3 (.clk(in_2), .D(or_2_out), .Q(d_ff_3_q));  // open: Qn, preset, en, reset
endmodule

module Seq_4 (
  input  X,
  input  in_2,
  output Z
);

  wire and_1_out, and_2_out, and_3_out, and_4_out, and_5_out, and_6_out, and_7_out, d_ff_1_q, d_ff_2_q,
       d_ff_3_q, not_1_out, not_2_out, not_3_out, not_4_out, not_5_out, not_6_out, not_7_out, not_8_out,
       not_9_out, or_2_out, or_3_out;

  not not_1 (not_1_out, X);
  not not_2 (not_2_out, X);
  not not_3 (not_3_out, d_ff_3_q);
  not not_4 (not_4_out, d_ff_1_q);
  not not_5 (not_5_out, d_ff_2_q);
  not not_6 (not_6_out, X);
  not not_7 (not_7_out, d_ff_1_q);
  not not_8 (not_8_out, d_ff_3_q);
  not not_9 (not_9_out, X);
  and and_1 (and_1_out, d_ff_1_q, not_1_out);
  and and_2 (and_2_out, d_ff_1_q, d_ff_2_q);
  and and_3 (and_3_out, d_ff_2_q, d_ff_3_q, not_2_out);
  and and_4 (and_4_out, d_ff_3_q, X);
  and and_5 (and_5_out, d_ff_2_q, not_3_out);
  and and_6 (and_6_out, not_4_out, not_5_out, not_6_out);
  and and_7 (and_7_out, not_7_out, not_8_out, not_9_out);
  or or_1 (Z, and_1_out, and_2_out);
  or or_2 (or_2_out, and_4_out, and_5_out);
  or or_3 (or_3_out, and_6_out, and_7_out);
  D_Flip_Flop d_ff_1 (.clk(in_2), .D(and_3_out), .Q(d_ff_1_q));  // open: Qn, preset, en, reset
  D_Flip_Flop d_ff_2 (.clk(in_2), .D(or_2_out), .Q(d_ff_2_q));  // open: Qn, preset, en, reset
  D_Flip_Flop d_ff_3 (.clk(in_2), .D(or_3_out), .Q(d_ff_3_q));  // open: Qn, preset, en, reset
endmodule

module sequential_2 (
  input  _0,
  input  _1,
  input  _2,
  input  _3,
  input  _4,
  input  _5,
  input  _6,
  input  _7,
  input  _8,
  input  _9,
  output out_11
);

  wire _10_to_4_bit_out_11, _10_to_4_bit_out_12, _10_to_4_bit_out_13, _10_to_4_bit_out_14, clock_2_out,
       or_1_out, seq_1_1_z, seq_2_1_z, seq_3_1_z, seq_4_1_z;

  Clock clock_1 ();  // open: out
  // Buffer buffer_1 is placed but not wired
  Clock #(.highDuration(5), .lowDuration(5)) clock_2 (.out(clock_2_out));
  _16_4_priority_Encoder _10_to_4_bit (
    ._0(_0), ._1(_1), ._2(_2), ._3(_3), ._4(_4), ._5(_5), ._6(_6), ._7(_7), ._8(_8), ._9(_9),
    .out_11(_10_to_4_bit_out_11), .out_12(_10_to_4_bit_out_12), .out_13(_10_to_4_bit_out_13),
    .out_14(_10_to_4_bit_out_14));
  or or_1 (or_1_out, _10_to_4_bit_out_14, _10_to_4_bit_out_13, _10_to_4_bit_out_12, _10_to_4_bit_out_11);
  Seq_1 seq_1_1 (.X(_10_to_4_bit_out_11), .in_2(clock_2_out), .Z(seq_1_1_z));
  Seq_2 seq_2_1 (.X(_10_to_4_bit_out_12), .in_2(clock_2_out), .Z(seq_2_1_z));
  Seq_3 seq_3_1 (.X(_10_to_4_bit_out_13), .in_2(clock_2_out), .Z(seq_3_1_z));
  Seq_4 seq_4_1 (.X(_10_to_4_bit_out_14), .in_2(clock_2_out), .Z(seq_4_1_z));
  and and_1 (out_11, seq_1_1_z, seq_2_1_z, seq_3_1_z, seq_4_1_z);
endmodule

module Counter (
  input  X,
  input  in_2,
  output Z
);

  wire and_2_out, and_3_out, and_4_out, and_5_out, and_6_out, and_7_out, and_8_out, and_9_out, d_ff_1_q,
       d_ff_2_q, d_ff_3_q, not_1_out, not_2_out, not_3_out, not_4_out, not_5_out, not_6_out, not_7_out,
       not_8_out, or_1_out, or_2_out, or_3_out;

  and and_1 (Z, d_ff_1_q, d_ff_3_q, X);
  not not_1 (not_1_out, d_ff_3_q);
  not not_2 (not_2_out, X);
  not not_3 (not_3_out, d_ff_1_q);
  not not_4 (not_4_out, d_ff_2_q);
  not not_5 (not_5_out, d_ff_3_q);
  not not_6 (not_6_out, X);
  not not_7 (not_7_out, d_ff_3_q);
  not not_8 (not_8_out, X);
  and and_2 (and_2_out, d_ff_2_q, d_ff_3_q, X);
  and and_3 (and_3_out, d_ff_1_q, not_1_out);
  and and_4 (and_4_out, d_ff_1_q, not_2_out);
  and and_5 (and_5_out, not_3_out, not_4_out, d_ff_3_q, X);
  and and_6 (and_6_out, d_ff_2_q, not_5_out);
  and and_7 (and_7_out, d_ff_2_q, not_6_out);
  and and_8 (and_8_out, not_7_out, X);
  and and_9 (and_9_out, d_ff_3_q, not_8_out);
  or or_1 (or_1_out, and_2_out, and_3_out, and_4_out);
  or or_2 (or_2_out, and_5_out, and_6_out, and_7_out);
  or or_3 (or_3_out, and_8_out, and_9_out);
  D_Flip_Flop d_ff_1 (.clk(in_2), .D(or_1_out), .Q(d_ff_1_q));  // open: Qn, preset, en, reset
  D_Flip_Flop d_ff_2 (.clk(in_2), .D(or_2_out), .Q(d_ff_2_q));  // open: Qn, preset, en, reset
  D_Flip_Flop d_ff_3 (.clk(in_2), .D(or_3_out), .Q(d_ff_3_q));  // open: Qn, preset, en, reset
endmodule

module Counter_2 (
  input  in_1,
  input  in_2,
  output out_3
);

  wire d_ff_1_q, d_ff_2_q, d_ff_3_q, d_ff_4_q, d_ff_5_q;

  D_Flip_Flop d_ff_1 (.clk(in_1), .D(in_1), .Q(d_ff_1_q), .reset(in_2));  // open: Qn, preset, en
  D_Flip_Flop d_ff_2 (.clk(in_1), .D(d_ff_1_q), .Q(d_ff_2_q), .reset(in_2));  // open: Qn, preset, en
  D_Flip_Flop d_ff_3 (.clk(in_1), .D(d_ff_2_q), .Q(d_ff_3_q), .reset(in_2));  // open: Qn, preset, en
  D_Flip_Flop d_ff_4 (.clk(in_1), .D(d_ff_3_q), .Q(d_ff_4_q), .reset(in_2));  // open: Qn, preset, en
  D_Flip_Flop d_ff_5 (.clk(in_1), .D(d_ff_4_q), .Q(d_ff_5_q), .reset(in_2));  // open: Qn, preset, en
  D_Flip_Flop d_ff_6 (.clk(in_1), .D(d_ff_5_q), .Q(out_3), .reset(in_2));  // open: Qn, preset, en
endmodule

module Pattern_checker (
  input  in_1,
  input  in_2,
  input  in_3,
  input  in_4,
  input  in_5,
  input  in_6,
  input  in_7,
  input  in_8,
  input  in_9,
  input  in_10,
  input  in_11,
  input  in_12,
  input  in_13,
  input  in_14,
  input  in_15,
  input  in_16,
  input  in_17,
  input  in_18,
  input  in_19,
  input  in_20,
  input  in_21,
  input  in_22,
  output out_23
);

  wire d_ff_1_q, d_ff_2_q, d_ff_3_q, d_ff_4_q, d_ff_5_q, d_ff_6_q, d_ff_7_q, d_ff_8_q, d_ff_9_q, d_ff_10_q,
       n4_bit_comparator_1_out_10, n4_bit_comparator_2_out_10, n4_bit_comparator_3_out_10,
       n4_bit_comparator_4_out_10, n4_bit_comparator_5_out_10, or_1_out, or_gate_1_out_6;

  _4_bit_comparator u_4_bit_comparator_1 (
    .A(in_19), .B(in_20), .C(in_21), .D(in_22), .a_2(1'b0), .b_2(1'b1), .E(d_ff_1_q), .c_2(1'b1), .d_2(1'b1),
    .out_10(n4_bit_comparator_1_out_10));
  D_Flip_Flop d_ff_1 (.clk(in_1), .D(in_1), .Q(d_ff_1_q), .reset(or_gate_1_out_6));  // open: Qn, preset, en
  or or_1 (or_1_out, n4_bit_comparator_1_out_10, n4_bit_comparator_2_out_10, n4_bit_comparator_3_out_10, n4_bit_comparator_4_out_10, n4_bit_comparator_5_out_10);
  D_Flip_Flop #(.trigger("falling")) d_ff_2 (
    .clk(in_1), .D(or_1_out), .Q(d_ff_2_q), .reset(in_2));  // open: Qn, preset, en
  D_Flip_Flop d_ff_3 (.clk(in_1), .D(d_ff_1_q), .Q(d_ff_3_q), .reset(in_2));  // open: Qn, preset, en
  Or_gate or_gate_1 (
    .in_1(d_ff_3_q), .in_2(d_ff_5_q), .in_3(in_2), .in_4(d_ff_6_q), .in_5(d_ff_8_q), .out_6(or_gate_1_out_6));
  _4_bit_comparator u_4_bit_comparator_2 (
    .A(in_3), .B(in_4), .C(in_5), .D(in_6), .a_2(1'b0), .b_2(1'b1), .E(d_ff_3_q), .c_2(1'b1), .d_2(1'b0),
    .out_10(n4_bit_comparator_2_out_10));
  D_Flip_Flop #(.trigger("falling")) d_ff_4 (
    .clk(in_1), .D(d_ff_2_q), .Q(d_ff_4_q), .reset(in_2));  // open: Qn, preset, en
  D_Flip_Flop d_ff_5 (.clk(in_1), .D(d_ff_3_q), .Q(d_ff_5_q), .reset(in_2));  // open: Qn, preset, en
  _4_bit_comparator u_4_bit_comparator_3 (
    .A(in_7), .B(in_8), .C(in_9), .D(in_10), .a_2(1'b0), .b_2(1'b0), .E(d_ff_5_q), .c_2(1'b1), .d_2(1'b0),
    .out_10(n4_bit_comparator_3_out_10));
  and and_1 (out_23, d_ff_2_q, d_ff_4_q, d_ff_7_q, d_ff_9_q, d_ff_10_q);
  D_Flip_Flop d_ff_6 (.clk(in_1), .D(d_ff_5_q), .Q(d_ff_6_q), .reset(in_2));  // open: Qn, preset, en
  D_Flip_Flop #(.trigger("falling")) d_ff_7 (
    .clk(in_1), .D(d_ff_4_q), .Q(d_ff_7_q), .reset(in_2));  // open: Qn, preset, en
  D_Flip_Flop d_ff_8 (.clk(in_1), .D(d_ff_6_q), .Q(d_ff_8_q), .reset(in_2));  // open: Qn, preset, en
  _4_bit_comparator u_4_bit_comparator_4 (
    .A(in_11), .B(in_12), .C(in_13), .D(in_14), .a_2(1'b0), .b_2(1'b1), .E(d_ff_6_q), .c_2(1'b1), .d_2(1'b0),
    .out_10(n4_bit_comparator_4_out_10));
  D_Flip_Flop #(.trigger("falling")) d_ff_9 (
    .clk(in_1), .D(d_ff_7_q), .Q(d_ff_9_q), .reset(in_2));  // open: Qn, preset, en
  _4_bit_comparator u_4_bit_comparator_5 (
    .A(in_15), .B(in_16), .C(in_17), .D(in_18), .a_2(1'b0), .b_2(1'b1), .E(d_ff_8_q), .c_2(1'b0), .d_2(1'b0),
    .out_10(n4_bit_comparator_5_out_10));
  D_Flip_Flop #(.trigger("falling")) d_ff_10 (
    .clk(in_1), .D(d_ff_9_q), .Q(d_ff_10_q), .reset(in_2));  // open: Qn, preset, en
endmodule

module Or_gate (
  input  in_1,
  input  in_2,
  input  in_3,
  input  in_4,
  input  in_5,
  output out_6
);

  wire nor_1_out;

  nor nor_1 (nor_1_out, in_1, in_2, in_3, in_4, in_5);
  nor nor_2 (out_6, nor_1_out, nor_1_out);
endmodule
