// Logisim project Part-1 Combinational Logic Circuit.circ as structural Verilog: 3 circuits, main circuit main
module main (
);

  wire _0_out, _1_out, _2_out, _3_out, _4_out, _5_out, _6_out, _7_out, _8_out, _9_out,
       Binary_to_7_Segment_a_2, Binary_to_7_Segment_b_2, Binary_to_7_Segment_c_2, Binary_to_7_Segment_d_2,
       Binary_to_7_Segment_e, Binary_to_7_Segment_f, Binary_to_7_Segment_g, decimal_to_binary_done_1_a,
       decimal_to_binary_done_1_b, decimal_to_binary_done_1_c, decimal_to_binary_done_1_d;

  Button _0 (.out(_0_out));
  Button _1 (.out(_1_out));
  Button _4 (.out(_4_out));
  Button _3 (.out(_3_out));
  Button _7 (.out(_7_out));
  Button _6 (.out(_6_out));
  Button _9 (.out(_9_out));
  Button _2 (.out(_2_out));
  Button _5 (.out(_5_out));
  Button _8 (.out(_8_out));
  Decimal_to_Binary_Done decimal_to_binary_done_1 (
    ._0(_0_out), ._1(_1_out), ._2(_2_out), ._3(_3_out), ._4(_4_out), ._5(_5_out), ._6(_6_out), ._7(_7_out),
    ._8(_8_out), ._9(_9_out), .D(decimal_to_binary_done_1_d), .C(decimal_to_binary_done_1_c),
    .B(decimal_to_binary_done_1_b), .A(decimal_to_binary_done_1_a));
  _7_Segment_Display u_7_segment_display_1 (
    .g(Binary_to_7_Segment_g), .f(Binary_to_7_Segment_f), .a(Binary_to_7_Segment_a_2),
    .b(Binary_to_7_Segment_b_2), .e(Binary_to_7_Segment_e), .d(Binary_to_7_Segment_d_2),
    .c(Binary_to_7_Segment_c_2));  // open: dp
  _4_Bit_Binary_to_7_Segment Binary_to_7_Segment (
    .D(decimal_to_binary_done_1_d), .C(decimal_to_binary_done_1_c), .B(decimal_to_binary_done_1_b),
    .A(decimal_to_binary_done_1_a), .g(Binary_to_7_Segment_g), .f(Binary_to_7_Segment_f),
    .e(Binary_to_7_Segment_e), .d_2(Binary_to_7_Segment_d_2), .c_2(Binary_to_7_Segment_c_2),
    .b_2(Binary_to_7_Segment_b_2), .a_2(Binary_to_7_Segment_a_2));

  // Notes on the sheet:
  //   KEYPAD
endmodule

// Decimal to BCD
module Decimal_to_Binary_Done (
  input  _0,
  input  _1,
  input  _2,
  input  _3,
  input  _4,
  input  _5,
  input  _6,
  input  _7,
  input  _8,
  input  _9,
  output D,
  output C,
  output B,
  output A
);

  or u_A (A, _0, _2, _4, _6, _8);
  or u_B (B, _1, _2, _5, _6, _9);
  or u_C (C, _3, _4, _5, _6);
  or u_D (D, _7, _8, _9);

  // Notes on the sheet:
  //   Decimal to Binary Conversion
endmodule

// Segment-1
module _4_Bit_Binary_to_7_Segment (
  input  D,
  input  C,
  input  B,
  input  A,
  output g,
  output f,
  output e,
  output d_2,
  output c_2,
  output b_2,
  output a_2
);

  wire and_1_out, and_2_out, and_3_out, and_4_out, and_5_out, and_6_out, and_7_out, and_8_out, and_9_out,
       and_10_out, and_11_out, and_12_out, and_13_out, and_14_out, and_15_out, and_16_out, and_17_out,
       and_18_out, and_19_out, and_20_out, not_1_out, not_2_out, not_3_out, not_4_out, not_5_out, not_6_out,
       not_7_out, not_8_out, not_9_out, not_10_out, not_11_out, or_1_out, or_3_out, or_4_out, or_6_out,
       or_7_out, or_8_out, or_9_out, or_10_out, or_11_out, or_12_out, or_13_out;

  and and_1 (and_1_out, B, A);
  and and_2 (and_2_out, D, A);
  and and_3 (and_3_out, D, B);
  not not_1 (not_1_out, B);
  and and_4 (and_4_out, not_1_out, A);
  and and_5 (and_5_out, C, B);
  not not_2 (not_2_out, C);
  and and_6 (and_6_out, not_2_out, A);
  and and_7 (and_7_out, B, A);
  not not_3 (not_3_out, C);
  and and_8 (and_8_out, not_3_out, A);
  and and_9 (and_9_out, C, not_4_out);
  not not_4 (not_4_out, A);
  and and_10 (and_10_out, C, B);
  and and_11 (and_11_out, D, B);
  not not_5 (not_5_out, B);
  and and_12 (and_12_out, not_5_out, A);
  and and_13 (and_13_out, B, not_6_out);
  not not_6 (not_6_out, A);
  not not_7 (not_7_out, C);
  and and_14 (and_14_out, not_7_out, A);
  not not_8 (not_8_out, C);
  and and_15 (and_15_out, not_8_out, B);
  and and_16 (and_16_out, C, not_9_out);
  not not_9 (not_9_out, B);
  not not_10 (not_10_out, C);
  and and_17 (and_17_out, not_10_out, A);
  and and_18 (and_18_out, C, not_11_out);
  not not_11 (not_11_out, A);
  and and_19 (and_19_out, C, B);
  or or_1 (or_1_out, and_1_out, C);
  or or_2 (g, or_1_out, or_3_out);
  or or_3 (or_3_out, and_2_out, and_3_out);
  or or_4 (or_4_out, and_4_out, and_5_out);
  and and_20 (and_20_out, D, B);
  or or_5 (e, and_6_out, and_7_out);
  or or_6 (or_6_out, and_8_out, and_9_out);
  or or_7 (or_7_out, and_10_out, and_11_out);
  or or_8 (or_8_out, and_12_out, and_13_out);
  or or_9 (or_9_out, C, D);
  or or_10 (or_10_out, and_14_out, and_15_out);
  or or_11 (or_11_out, and_16_out, D);
  or or_12 (or_12_out, and_17_out, and_18_out);
  or or_13 (or_13_out, and_19_out, D);
  or or_14 (f, or_4_out, and_20_out);
  or or_15 (d_2, or_6_out, or_7_out);
  or or_16 (c_2, or_8_out, or_9_out);
  or or_17 (b_2, or_10_out, or_11_out);
  or or_18 (a_2, or_12_out, or_13_out);

  // Notes on the sheet:
  //   4 Bit Binary to 7 Segment
endmodule
